# Fritzing sketch diagram_exam_2 (saved by Fritzing 0.9.3b)
breadboards: 1

parts:
  Part1 = Arduino Uno (Rev3) - ICSP
  LCD1 = LCD screen
  Part2 = Thumb Joystick
  R1 = Trimmer Potentiometer [maximum_resistance=10kΩ package=THT]
  S1 = Momentary Switch [package=ksa_sealed_tac_switch]
  R2 = Resistor [tolerance=±5% resistance=10k package="0805 [SMD]"]
  S2 = Momentary Switch [package=ksa_sealed_tac_switch]
  R3 = Resistor [tolerance=±5% resistance=10k package="0805 [SMD]"]
  S3 = Momentary Switch [package=ksa_sealed_tac_switch]
  R4 = Resistor [tolerance=±5% resistance=10k package="0805 [SMD]"]
  S4 = Momentary Switch [package=ksa_sealed_tac_switch]
  R5 = Resistor [tolerance=±5% resistance=10k package="0805 [SMD]"]

nets:
  N1: Part1.A0, R1.wiper
  N2: Part1.A1, Part2.VERT
  N3: Part1.A2, Part2.HORZ
  N4: Part1.D8, LCD1.E
  N5: Part1.D9_PWM, LCD1.DB4
  N6: Part1.D10_PWM/SS, LCD1.DB5
  N7: Part1.D11_PWM/MOSI, LCD1.DB6
  N8: Part1.D12/MISO, LCD1.DB7
  N9: Part1.D3_PWM, S4.3
  N10: Part1.D4, S3.3
  N11: Part1.D5_PWM, S2.3
  N12: Part1.D6_PWM, S1.3
  N13: Part1.D7, LCD1.RS
  5V: Part1.5V, LCD1.VDD, LCD1.LED+, Part2.VCC, R1.leg1
  GND: Part1.GND, LCD1.VSS, LCD1.V0, LCD1.R/W, LCD1.LED-, Part2.GND, R1.leg2, R2.Pin_1, R3.Pin_1, R4.Pin_1, R5.Pin_1
  N14: S1.1, R2.Pin_0
  N15: S2.1, R3.Pin_0
  N16: S3.1, R4.Pin_0
  N17: S4.1, R5.Pin_0
